# Fritzing sketch 4 voltage regulator (saved by Fritzing 0.9.3b)
circuit board: 2.66751cm x 1.31744cm
breadboards: 1

parts:
  RL = Resistor [tolerance=±5% resistance=470 package="0805 [SMD]"]
  RH = Resistor [tolerance=±5% resistance=220 package="0805 [SMD]"]
  J2 = Screw terminal - 2 pins [package=THT]
  J3 = Screw terminal - 2 pins [package=THT]
  LM317 = Voltage Regulator [package=to220-adj]
  C2_1000uf/16v = Capacitor Polarized [package=cpol-radial-10uf-25v]
  C1_0_1uf/16v = Capacitor Polarized [package=cpol-radial-10uf-25v]

nets:
  N1: RL.Pin_0, RH.Pin_1, LM317.ADJ
  GND: RL.Pin_1, J2.pin1, J3.pin2, C2_1000uf/16v.-, C1_0_1uf/16v.-
  4V: RH.Pin_0, J3.pin1, LM317.OUT, C2_1000uf/16v.+
  9V: J2.pin2, LM317.IN, C1_0_1uf/16v.+

notes:
  LM317 calc out voltage
  Vref = 1,25 V
  RL = 470 Ohm
  RH = 220 Ohm
  Vout = Vref x ( 1 + RL / RH )
  Vout ~= 3,92 V
  C2 is for fix 1,5 A out to 2 A.
